// Logisim project FSM.circ as structural Verilog: 8 circuits, main circuit FSM
module FSM (
  input  FSM_Input,
  output out_2
);

  wire clock_1_out;
  wire [1:0] fsmlogic_1_next_state, register_1_q;

  Register #(.width(2)) register_1 (.D(fsmlogic_1_next_state), .clk(clock_1_out), .Q(register_1_q));  // open: en, clr
  Clock clock_1 (.out(clock_1_out));
  FSMLogic fsmlogic_1 (
    .Input_Bit(FSM_Input), .Current_State(register_1_q), .Output(out_2), .Next_State(fsmlogic_1_next_state));
endmodule

// FSM Logic
module FSMLogic (
  input  Input_Bit,
  input  [1:0] Current_State,
  output Output,
  output [1:0] Next_State
);

  wire and_1_out, and_2_out, not_1_out, not_2_out, not_3_out;

  not not_1 (not_1_out, Current_State[1]);
  not not_2 (not_2_out, Input_Bit);
  not not_3 (not_3_out, Current_State[0]);
  and and_1 (and_1_out, Input_Bit, not_1_out);
  or or_1 (Output, and_1_out, and_2_out);
  and and_2 (and_2_out, not_2_out, not_3_out);
  StateBitZero statebitzero_1 (
    .Input(Input_Bit), .State_Bit_0(Current_State[0]), .State_Bit_1(Current_State[1]),
    .New_State_0(Next_State[0]));
  StateBitOne statebitone_1 (
    .Input(Input_Bit), .State_Bit_0(Current_State[0]), .State_Bit_1(Current_State[1]),
    .New_State_1(Next_State[1]));

  // Other names for the same wires on the sheet: Currrent_State_0 = Current_State[0];
  //   Current_State_1 = Current_State[1]
endmodule

// State Bit 1
module StateBitOne (
  input  Input,
  input  State_Bit_0,
  input  State_Bit_1,
  output New_State_1
);

  // NOT_Gate not_1 has open pins: in=Input, out=open
  // NOT_Gate not_2 has open pins: in=State_Bit_0, out=open
  // NOT_Gate not_3 has open pins: in=State_Bit_1, out=open
  or or_1 (New_State_1, Input, State_Bit_0);

  // Notes on the sheet:
  //   PUT CIRCUITRY HERE
endmodule

// State Bit 0
module StateBitZero (
  input  Input,
  input  State_Bit_0,
  input  State_Bit_1,
  output New_State_0
);

  wire not_4_out;

  // NOT_Gate not_1 has open pins: in=Input, out=open
  // NOT_Gate not_2 has open pins: in=State_Bit_0, out=open
  // NOT_Gate not_3 has open pins: in=State_Bit_1, out=open
  not not_4 (not_4_out, Input);
  or or_1 (New_State_0, not_4_out, State_Bit_1);

  // Notes on the sheet:
  //   PUT CIRCUITRY HERE
endmodule

module EX4 (
  input  [7:0] In1,
  output Out1,
  output [7:0] Out2
);

  and and_1 (Out1, In1[0], In1[7]);
  not not_1 (Out2[1], In1[1]);
  not not_2 (Out2[2], In1[2]);
  not not_3 (Out2[3], In1[3]);
  not not_4 (Out2[4], In1[4]);
  not not_5 (Out2[5], In1[5]);
  not not_6 (Out2[6], In1[6]);
  not not_7 (Out2[7], In1[7]);

  assign Out2[0] = In1[0];
endmodule

module rotr (
  input  [15:0] in_1,
  input  [7:0] in_2,
  input  [3:0] in_3
);

  wire clock_1_out;
  wire [7:0] adder_1_out, register_1_q;

  Adder adder_1 (.a(in_2), .b(register_1_q), .out(adder_1_out));  // open: cin, cout
  Clock clock_1 (.out(clock_1_out));
  SL sl_1 (.in_1(in_1));  // open: out_2
  Register register_1 (.D(adder_1_out), .clk(clock_1_out), .Q(register_1_q));  // open: en, clr
endmodule

module SL (
  input  [15:0] in_1,
  output [15:0] out_2
);


  assign out_2 = {in_1[0], in_1[15:1]};
endmodule

module Equal4Bit (
  input  [3:0] in_1,
  input  [7:0] in_2,
  output out_3
);

  wire and_1_out, and_2_out, xnor_1_out, xnor_2_out, xnor_3_out, xnor_4_out;

  xnor xnor_1 (xnor_1_out, in_1[0], in_2[0]);
  xnor xnor_2 (xnor_2_out, in_1[1], in_2[1]);
  xnor xnor_3 (xnor_3_out, in_1[2], in_2[2]);
  xnor xnor_4 (xnor_4_out, in_1[3], in_2[3]);
  and and_1 (and_1_out, xnor_1_out, xnor_2_out);
  and and_2 (and_2_out, xnor_3_out, xnor_4_out);
  and and_3 (out_3, and_1_out, and_2_out);
endmodule
