// Logisim project lab05.circ as structural Verilog: 7 circuits, main circuit main
module main (
  input  [7:0] in_1,
  output [7:0] out_2,
  output [7:0] out_3
);

  AddMachine addmachine_1 (.in_1(in_1), .out_2(out_2), .out_3(out_3));
endmodule

module NAND1 (
  input  in_1,
  input  in_2,
  output out_3
);

  and and_1 (out_3, in_1, in_2);
endmodule

module XOR1 (
  input  in_1,
  input  in_2,
  output out_3
);

  wire and_1_out, and_2_out, not_1_out, not_2_out;

  not not_1 (not_1_out, in_1);
  not not_2 (not_2_out, in_2);
  and and_1 (and_1_out, in_1, not_2_out);
  and and_2 (and_2_out, not_1_out, in_2);
  or or_1 (out_3, and_1_out, and_2_out);
endmodule

module NOR1 (
  input  in_1,
  input  in_2,
  output out_3
);

  wire or_1_out;

  or or_1 (or_1_out, in_1, in_2);
  not not_1 (out_3, or_1_out);
endmodule

module MUX2_1 (
  input  s,
  input  b,
  input  a,
  output out_4
);

  wire and_1_out, and_2_out, not_1_out;

  and and_1 (and_1_out, b, s);
  and and_2 (and_2_out, a, not_1_out);
  not not_1 (not_1_out, s);
  or or_1 (out_4, and_1_out, and_2_out);
endmodule

module MUX4_1 (
  input  s0,
  input  s1,
  input  d,
  input  c,
  input  b,
  input  a,
  output out_7
);

  wire mux2_1_1_out_4, mux2_1_2_out_4;

  MUX2_1 mux2_1_1 (.s(s0), .b(d), .a(c), .out_4(mux2_1_1_out_4));
  MUX2_1 mux2_1_2 (.s(s0), .b(b), .a(a), .out_4(mux2_1_2_out_4));
  MUX2_1 mux2_1_3 (.s(s1), .b(mux2_1_1_out_4), .a(mux2_1_2_out_4), .out_4(out_7));
endmodule

module AddMachine (
  input  [7:0] in_1,
  output [7:0] out_2,
  output [7:0] out_3
);

  wire clock_1_out;

  Clock clock_1 (.out(clock_1_out));
  Adder adder_1 (.a(in_1), .b(out_3), .out(out_2));  // open: cin, cout
  Register register_1 (.D(out_2), .clk(clock_1_out), .Q(out_3));  // open: en, clr
endmodule
