// Logisim project alu.circ as structural Verilog: 2 circuits, main circuit alu
module alu (
  input  [31:0] A,
  input  [31:0] B,
  input  [3:0] ALUSel,
  output [31:0] Result
);

  wire [0:0] slt1;
  wire [31:0] add, and1, divu, mul, mulh1, mulhu, or1, remu, sll1, sra1, srl1, sub, xor1;

  Adder #(.width(32)) adder_1 (.a(A), .b(B), .out(add));  // open: cin, cout
  Subtractor #(.width(32)) subtractor_1 (.a(A), .b(B), .out(sub));  // open: bin, bout
  assign and1 = A & B;  // AND_Gate and_1, 32 bits wide
  assign or1 = A | B;  // OR_Gate or_1, 32 bits wide
  assign xor1 = A ^ B;  // XOR_Gate xor_1, 32 bits wide
  Multiplier #(.width(32)) multiplier_1 (.a(A), .b(B), .out(mul), .cout(mulhu));  // open: cin
  Shifter #(.width(32), .shift("lr")) shifter_1 (.in(A), .\dist (B[4:0]), .out(srl1));
  Shifter #(.width(32), .shift("ar")) shifter_2 (.in(A), .\dist (B[4:0]), .out(sra1));
  Shifter #(.width(32)) shifter_3 (.in(A), .\dist (B[4:0]), .out(sll1));
  Comparator #(.width(32)) comparator_1 (.a(A), .b(B), .lt(slt1[0]));  // open: gt, eq
  Divider #(.width(32)) divider_1 (.a(A), .b(B), .out(divu), .rem(remu));  // open: upper
  mulh mulh_1 (.in_1(A), .in_2(B), .out_3(mulh1));
  Multiplexer #(.select(4), .width(32), .enable("false")) multiplexer_1 (
    .in0(add), .in1(and1), .in2(or1), .in3(xor1), .in4(srl1), .in5(sra1), .in6(sll1),
    .in7({{31{1'b0}}, slt1[0]}), .in8(divu), .in9(remu), .in10(mul), .in11(mulhu), .in12(sub), .in13(B),
    .in14(mulh1), .out(Result), .sel(ALUSel));  // open: in15

  // Other names for the same wires on the sheet: bsel[31:0] = B

  // Notes on the sheet:
  //   INPUTS to your circuit
  //   DON'T CHANGE THE LOCATIONS OF THE INPUTS AND OUTPUTS!
  //   OUTPUT from your circuit
endmodule

module mulh (
  input  [31:0] in_1,
  input  [31:0] in_2,
  output [31:0] out_3
);

  wire [30:0] adder_1_out, adder_2_out, adder_3_out, adder_4_out, not_1_out, not_2_out, not_3_out, not_4_out;
  wire [31:0] multiplier_2_cout, multiplier_3_cout, not_5_out, not_6_out, result1, result2, result3, result4;

  assign not_1_out = ~in_1[30:0];  // NOT_Gate not_1, 31 bits wide
  assign not_2_out = ~in_2[30:0];  // NOT_Gate not_2, 31 bits wide
  assign not_3_out = ~in_1[30:0];  // NOT_Gate not_3, 31 bits wide
  Adder #(.width(31)) adder_1 (.a(not_3_out), .b(31'h1), .out(adder_1_out));  // open: cin, cout
  assign not_4_out = ~in_2[30:0];  // NOT_Gate not_4, 31 bits wide
  Adder #(.width(31)) adder_2 (.a(not_4_out), .b(31'h1), .out(adder_2_out));  // open: cin, cout
  Multiplier #(.width(32)) multiplier_1 (
    .a({1'b0, in_1[30:0]}), .b({1'b0, in_2[30:0]}), .cout(result1));  // open: out, cin
  Adder #(.width(31)) adder_3 (.a(not_1_out), .b(31'h1), .out(adder_3_out));  // open: cin, cout
  Adder #(.width(31)) adder_4 (.a(not_2_out), .b(31'h1), .out(adder_4_out));  // open: cin, cout
  Multiplier #(.width(32)) multiplier_2 (
    .a({1'b0, adder_1_out}), .b({1'b0, in_2[30:0]}), .cout(multiplier_2_cout));  // open: out, cin
  Multiplier #(.width(32)) multiplier_3 (
    .a({1'b0, adder_2_out}), .b({1'b0, in_1[30:0]}), .cout(multiplier_3_cout));  // open: out, cin
  Multiplier #(.width(32)) multiplier_4 (
    .a({1'b0, adder_3_out}), .b({1'b0, adder_4_out}), .cout(result4));  // open: out, cin
  assign not_5_out = ~multiplier_2_cout;  // NOT_Gate not_5, 32 bits wide
  assign not_6_out = ~multiplier_3_cout;  // NOT_Gate not_6, 32 bits wide
  assign result2 = not_5_out | 32'h80000000;  // OR_Gate or_1, 32 bits wide
  assign result3 = not_6_out | 32'h80000000;  // OR_Gate or_2, 32 bits wide
  Multiplexer #(.select(2), .width(32), .enable("false")) multiplexer_1 (
    .in0(result1), .in1(result2), .in2(result3), .in3(result4), .out(out_3), .sel({in_2[31], in_1[31]}));

  // Other names for the same wires on the sheet: rem2[30:0] = in_2[30:0]; rem1[30:0] = in_1[30:0]; sign1 = in_1[31];
  //   sign2 = in_2[31]
endmodule
