// Logisim project cpu.circ as structural Verilog: 3 circuits, main circuit main
module main (
  input  [31:0] INSTRUCTION,
  input  in_2,
  output [31:0] FETCH_ADDRESS,
  output [31:0] ra,
  output [31:0] sp,
  output [31:0] t0,
  output [31:0] t1,
  output [31:0] t2,
  output [31:0] s0,
  output [31:0] s1,
  output [31:0] a0
);

  wire ASel, BrUn, BSel, comparator_1_eq, comparator_2_eq, comparator_2_lt, comparator_3_eq, comparator_3_lt,
       MemRW, multiplexer_4_out, multiplexer_5_out, PCSel, RegRW;
  wire [2:0] funct3, ImmSel, WBSel;
  wire [3:0] ALUSel;
  wire [6:0] INSTRUCTION2;
  wire [24:0] inst;
  wire [31:0] adder_1_out, ALUOut, bit_extender_1_out, bit_extender_2_out, imm, Memory, multiplexer_1_out,
       multiplexer_2_out, multiplexer_3_out, multiplexer_6_out, multiplexer_7_out, pc, PCplus4, RegData1,
       RegData2, register_1_q, wb;

  Adder #(.width(32)) adder_1 (.a(PCplus4), .b(32'h4), .out(adder_1_out));  // open: cin, cout
  Multiplexer #(.width(32), .enable("false")) multiplexer_1 (
    .in0(adder_1_out), .in1(ALUOut), .out(multiplexer_1_out), .sel(PCSel));
  Register #(.width(32)) u_PC (.D(multiplexer_1_out), .en(1'b1), .clk(in_2), .Q(PCplus4));  // open: clr
  Shifter #(.width(32), .shift("lr")) shifter_1 (.in(PCplus4), .\dist (5'b00010), .out(FETCH_ADDRESS));
  Multiplexer #(.width(32), .enable("false")) multiplexer_2 (
    .in0(INSTRUCTION), .in1(32'h13), .out(multiplexer_2_out), .sel(PCSel));
  Register #(.width(32)) register_1 (.D(FETCH_ADDRESS), .en(1'b1), .clk(in_2), .Q(register_1_q));  // open: clr
  Comparator #(.width(32)) comparator_1 (.a(INSTRUCTION), .b({32{1'b0}}), .eq(comparator_1_eq));  // open: gt, lt
  Shifter #(.width(32)) shifter_2 (.in(register_1_q), .\dist (5'b00010), .out(pc));
  Multiplexer #(.width(32), .enable("false")) multiplexer_3 (
    .in0(multiplexer_2_out), .in1(32'h13), .out(multiplexer_3_out), .sel(comparator_1_eq));
  Register #(.width(32)) register_2 (
    .D(multiplexer_3_out), .en(1'b1), .clk(in_2), .Q({inst[24:8], funct3, inst[4:0], INSTRUCTION2}));  // open: clr
  Comparator #(.width(32)) comparator_2 (
    .a(RegData1), .b(RegData2), .eq(comparator_2_eq), .lt(comparator_2_lt));  // open: gt
  Comparator #(.width(32), .mode("unsigned")) comparator_3 (
    .a(RegData1), .b(RegData2), .eq(comparator_3_eq), .lt(comparator_3_lt));  // open: gt
  Multiplexer #(.enable("false")) multiplexer_4 (
    .in0(comparator_2_lt), .in1(comparator_3_lt), .out(multiplexer_4_out), .sel(BrUn));
  Multiplexer #(.enable("false")) multiplexer_5 (
    .in0(comparator_2_eq), .in1(comparator_3_eq), .out(multiplexer_5_out), .sel(BrUn));
  regfile_main RegFile (
    .rs2(inst[17:13]), .rd(inst[4:0]), .Read_Data_1(RegData1), .Read_Data_2(RegData2), .ra(ra), .sp(sp),
    .t0(t0), .t1(t1), .t2(t2), .s0(s0), .s1(s1), .a0(a0), .rs1(inst[12:8]), .Write_Data(wb), .RegWEn(RegRW),
    .clk(in_2));
  Control control_1 (
    .instruction({inst[24:8], funct3, inst[4:0], INSTRUCTION2}), .BrLT(multiplexer_4_out),
    .BrEq(multiplexer_5_out), .WBSel(WBSel), .RegWEn(RegRW), .ALUSel(ALUSel), .MemRw(MemRW), .BSel(BSel),
    .ASel(ASel), .BrUn(BrUn), .ImmSel(ImmSel), .PCSel(PCSel));
  Multiplexer #(.width(32), .enable("false")) multiplexer_6 (
    .in0(RegData1), .in1(pc), .out(multiplexer_6_out), .sel(ASel));
  Multiplexer #(.width(32), .enable("false")) multiplexer_7 (
    .in0(RegData2), .in1(imm), .out(multiplexer_7_out), .sel(BSel));
  ImmediateGenerator immediategenerator_1 (.ImmSel(ImmSel), .InstIn({inst[24:8], funct3, inst[4:0]}), .out_3(imm));
  alu Arithmetic_Logic_Unit (.A(multiplexer_6_out), .B(multiplexer_7_out), .ALUSel(ALUSel), .Result(ALUOut));
  assign bit_extender_1_out = {{24{Memory[7]}}, Memory[7:0]};  // Bit_Extender bit_extender_1
  assign bit_extender_2_out = {{16{Memory[15]}}, Memory[15:0]};  // Bit_Extender bit_extender_2
  // mem_main DMEM: pin names not known; wires that end beside it: ALUOut, RegData2, MemRW, in_2, Memory
  Multiplexer #(.select(3), .width(32), .enable("false")) multiplexer_8 (
    .in0(PCplus4), .in1(ALUOut), .in2(bit_extender_1_out), .in3(bit_extender_2_out), .in4(Memory), .out(wb),
    .sel(WBSel));  // open: in5, in6, in7

  // Other names for the same wires on the sheet: clk = in_2; fetch_addr[31:0] = FETCH_ADDRESS;
  //   opcode[6:0] = INSTRUCTION2; INSTRUCTION2[31:7] = {inst[24:8], funct3, inst[4:0]}; rd[4:0] = inst[4:0];
  //   inst[7:5] = funct3; rs1[4:0] = inst[12:8]; rs2[4:0] = inst[17:13]

  // Notes on the sheet:
  //   Output
  //   Inputs/Outputs from run.circ. DO NOT MOVE THESE.
  //   Inputs
  //   Inputs/Outputs from run.circ. DO NOT MOVE THESE.
endmodule

module ImmediateGenerator (
  input  [2:0] ImmSel,
  input  [24:0] InstIn,
  output [31:0] out_3
);

  wire [31:0] bit_extender_1_out, bit_extender_2_out, bit_extender_3_out, bit_extender_4_out;

  assign bit_extender_1_out = {{20{InstIn[24]}}, InstIn[24:13]};  // Bit_Extender bit_extender_1
  assign bit_extender_2_out = {{20{InstIn[24]}}, {InstIn[24:18], InstIn[4:0]}};  // Bit_Extender bit_extender_2
  assign bit_extender_3_out = {{19{InstIn[24]}}, {InstIn[24], InstIn[0], InstIn[23:18], InstIn[4:1], 1'b0}};  // Bit_Extender bit_extender_3
  assign bit_extender_4_out = {{11{InstIn[24]}}, {InstIn[24], InstIn[12:5], InstIn[13], InstIn[23:14], 1'b0}};  // Bit_Extender bit_extender_4
  Multiplexer #(.select(3), .width(32), .enable("false")) multiplexer_1 (
    .in0(bit_extender_1_out), .in1(bit_extender_2_out), .in2(bit_extender_3_out),
    .in3({InstIn[24:5], {12{1'b0}}}), .in4(bit_extender_4_out), .out(out_3), .sel(ImmSel));  // open: in5, in6, in7
endmodule

module Control (
  input  [31:0] instruction,
  input  BrLT,
  input  BrEq,
  output [2:0] WBSel,
  output RegWEn,
  output [3:0] ALUSel,
  output MemRw,
  output BSel,
  output ASel,
  output BrUn,
  output [2:0] ImmSel,
  output PCSel
);

  wire comparator_1_eq, comparator_2_eq, comparator_3_eq, comparator_4_eq, comparator_5_eq, comparator_6_eq,
       comparator_7_eq, comparator_8_eq, comparator_9_eq, comparator_10_eq, comparator_11_eq,
       comparator_12_eq, comparator_13_eq, comparator_14_eq, comparator_15_eq, comparator_16_eq,
       multiplexer_1_out, multiplexer_2_out, multiplexer_3_out, multiplexer_4_out, multiplexer_5_out,
       multiplexer_6_out, not_1_out, or_2_out;
  wire [16:0] addr, multiplexer_7_out, multiplexer_8_out, multiplexer_9_out, multiplexer_10_out,
       multiplexer_11_out, multiplexer_12_out, multiplexer_13_out, multiplexer_14_out, multiplexer_15_out;

  ROM #(.addrWidth(17), .dataWidth(15)) rom_1 (
    .addr(addr), .data({ImmSel, BrUn, ASel, BSel, MemRw, ALUSel, RegWEn, WBSel}));
  Comparator #(.width(17)) comparator_1 (.a(addr), .b(17'h18c00), .eq(comparator_1_eq));  // open: gt, lt
  Comparator #(.width(17)) comparator_2 (.a(addr), .b(17'h18e00), .eq(comparator_2_eq));  // open: gt, lt
  Comparator #(.width(17)) comparator_3 (.a(addr), .b(17'h18f00), .eq(comparator_3_eq));  // open: gt, lt
  not not_1 (not_1_out, BrEq);
  Comparator #(.width(17)) comparator_4 (.a(addr), .b(17'h19c00), .eq(comparator_4_eq));  // open: gt, lt
  Multiplexer #(.enable("false")) multiplexer_1 (
    .in0(1'b0), .in1(BrEq), .out(multiplexer_1_out), .sel(comparator_1_eq));
  Multiplexer #(.enable("false")) multiplexer_2 (
    .in0(1'b0), .in1(BrLT), .out(multiplexer_2_out), .sel(comparator_2_eq));
  Multiplexer #(.enable("false")) multiplexer_3 (
    .in0(1'b0), .in1(BrLT), .out(multiplexer_3_out), .sel(comparator_3_eq));
  Comparator #(.width(17)) comparator_5 (.a(addr), .b(17'h18c80), .eq(comparator_5_eq));  // open: gt, lt
  Multiplexer #(.enable("false")) multiplexer_4 (
    .in0(1'b0), .in1(not_1_out), .out(multiplexer_4_out), .sel(comparator_5_eq));
  Comparator #(.width(17)) comparator_6 (.a(addr), .b(17'h1bc00), .eq(comparator_6_eq));  // open: gt, lt
  Multiplexer #(.enable("false")) multiplexer_5 (
    .in0(1'b0), .in1(1'b1), .out(multiplexer_5_out), .sel(comparator_6_eq));
  Multiplexer #(.enable("false")) multiplexer_6 (
    .in0(1'b0), .in1(1'b1), .out(multiplexer_6_out), .sel(comparator_4_eq));
  or or_1 (PCSel, multiplexer_1_out, multiplexer_2_out, multiplexer_3_out, multiplexer_4_out, multiplexer_5_out, multiplexer_6_out);
  Comparator #(.width(3)) comparator_7 (.a(instruction[14:12]), .b(3'b001), .eq(comparator_7_eq));  // open: gt, lt
  Comparator #(.width(3)) comparator_8 (.a(instruction[14:12]), .b(3'b101), .eq(comparator_8_eq));  // open: gt, lt
  Comparator #(.width(7)) comparator_9 (.a(instruction[6:0]), .b(7'b0100011), .eq(comparator_9_eq));  // open: gt, lt
  Comparator #(.width(7)) comparator_10 (.a(instruction[6:0]), .b(7'b1100011), .eq(comparator_10_eq));  // open: gt, lt
  Comparator #(.width(7)) comparator_11 (.a(instruction[6:0]), .b(7'b0110111), .eq(comparator_11_eq));  // open: gt, lt
  Comparator #(.width(7)) comparator_12 (.a(instruction[6:0]), .b(7'b1101111), .eq(comparator_12_eq));  // open: gt, lt
  Comparator #(.width(7)) comparator_13 (.a(instruction[6:0]), .b(7'b1100111), .eq(comparator_13_eq));  // open: gt, lt
  Comparator #(.width(7)) comparator_14 (.a(instruction[6:0]), .b(7'b0110011), .eq(comparator_14_eq));  // open: gt, lt
  Comparator #(.width(7)) comparator_15 (.a(instruction[6:0]), .b(7'b0000011), .eq(comparator_15_eq));  // open: gt, lt
  Comparator #(.width(7)) comparator_16 (.a(instruction[6:0]), .b(7'b0010011), .eq(comparator_16_eq));  // open: gt, lt
  or or_2 (or_2_out, comparator_7_eq, comparator_8_eq);
  Multiplexer #(.width(17), .enable("false")) multiplexer_7 (
    .in0({17{1'b0}}), .in1({instruction[6:0], instruction[14:12], {7{1'b0}}}), .out(multiplexer_7_out),
    .sel(comparator_9_eq));
  Multiplexer #(.width(17), .enable("false")) multiplexer_8 (
    .in0({17{1'b0}}), .in1({instruction[6:0], instruction[14:12], {7{1'b0}}}), .out(multiplexer_8_out),
    .sel(comparator_10_eq));
  Multiplexer #(.width(17), .enable("false")) multiplexer_9 (
    .in0({17{1'b0}}), .in1({instruction[6:0], {10{1'b0}}}), .out(multiplexer_9_out), .sel(comparator_11_eq));
  Multiplexer #(.width(17), .enable("false")) multiplexer_10 (
    .in0({17{1'b0}}), .in1({instruction[6:0], {10{1'b0}}}), .out(multiplexer_10_out), .sel(comparator_12_eq));
  Multiplexer #(.width(17), .enable("false")) multiplexer_11 (
    .in0({17{1'b0}}), .in1({instruction[6:0], instruction[14:12], instruction[31:25]}),
    .out(multiplexer_11_out), .sel(comparator_14_eq));
  Multiplexer #(.width(17), .enable("false")) multiplexer_12 (
    .in0({17{1'b0}}), .in1({instruction[6:0], instruction[14:12], {7{1'b0}}}), .out(multiplexer_12_out),
    .sel(comparator_15_eq));
  Multiplexer #(.width(17), .enable("false")) multiplexer_13 (
    .in0({instruction[6:0], instruction[14:12], {7{1'b0}}}),
    .in1({instruction[6:0], instruction[14:12], instruction[31:25]}), .out(multiplexer_13_out), .sel(or_2_out));
  Multiplexer #(.width(17), .enable("false")) multiplexer_14 (
    .in0({17{1'b0}}), .in1({instruction[6:0], instruction[14:12], {7{1'b0}}}), .out(multiplexer_14_out),
    .sel(comparator_13_eq));
  Multiplexer #(.width(17), .enable("false")) multiplexer_15 (
    .in0({17{1'b0}}), .in1(multiplexer_13_out), .out(multiplexer_15_out), .sel(comparator_16_eq));
  assign addr = multiplexer_11_out | multiplexer_12_out | multiplexer_15_out | multiplexer_7_out | multiplexer_8_out | multiplexer_9_out | multiplexer_10_out | multiplexer_14_out;  // OR_Gate or_3, 17 bits wide

  // Other names for the same wires on the sheet: funct3[2:0] = instruction[14:12]; opcode[6:0] = instruction[6:0];
  //   funct7[6:0] = instruction[31:25]; eq = BrEq; lt = BrLT

  // Notes on the sheet:
  //   contents of rom_1 (hex, n*v repeats v):
  //   3072*0 20a 127*0 20b 127*0 20c 16127*0 209 255*0 279 127*0 269 127*0 239 127*0 249 31*0 259 95*0 229
  //   127*0 219 15743*0 1300 16127*0 9 a9 30*0 c9 95*0 69 e9 126*0 79 128*0 b9 126*0 39 127*0 49 89 126*0
  //   29 127*0 19 99 3198*0 32d9 45055*0 2600 127*0 2600 383*0 2600 2600 254*0 2e00 3327*0 208 8191*0 4608
endmodule
